# Fritzing sketch MillePetitsGestes (saved by Fritzing 0.9.3b)
breadboards: 1

parts:
  IC2 = IC, DIP package, 20 pins [chip_label=SN74HCT245N]
  R2 = Resistor [tolerance=±5% resistance=390 package="0805 [SMD]"]
  C2 = Capacitor Polarized [package=cpol-radial-1000uf-25v]
  S1 = Pushbutton [package="[THT]"]
  U2 = lolin
  R3 = Resistor [tolerance=±5% resistance=390 package="0805 [SMD]"]
  JACK1 = 2.1mm Barrel Jack with Terminal Block
  NEOPIXEL2 = Neopixel Strip -- White (60/m) [part_number=1138]

nets:
  N1: IC2.pin1, IC2.pin10, IC2.pin19, R2.Pin_1, C2.-, U2.connector15, JACK1.NEG, NEOPIXEL2.GND
  N2: IC2.pin2, U2.connector22
  N3: IC2.pin18, R3.Pin_1
  N4: IC2.pin20, C2.+, S1.Pin_1, S1.Pin_2, U2.connector14, JACK1.POS, NEOPIXEL2.+5V
  N5: R2.Pin_0, S1.Pin_3, S1.Pin_4, U2.connector12
  N6: R3.Pin_0, NEOPIXEL2.DI

notes:
  Mille Petits Gestes / MP0804h
  Conception Derrick Giscloux, septembre 2018.
  • Les deux résistances sont de 390 ohms
  • les leds utilisées sont des grappes de 2812B individuelles

custom parts:
  Neopixel Strip -- White (60/m): Neopixel Strip, White, 60 pixels per meter.
